# Fritzing sketch BinaryThermometer (saved by Fritzing 0.9.3b)
breadboards: 1

parts:
  Part1 = Arduino Nano (Rev3.0)
  NEOPIXEL4 = Neopixel Strip -- Black (60/m) [part_number=1461]
  DS3 = DS18B20 1-Wire Temperature Sensor [part_number=DS18B20]
  R4 = Rotary Potentiometer (Large) [package=THT]
  R3 = Resistor [tolerance=±0.5% resistance=4.7k package=THT]

nets:
  GND: Part1.GND, NEOPIXEL4.GND, DS3.GND, R4.leg2
  N1: Part1.D5, DS3.DQ
  N2: Part1.D7, NEOPIXEL4.DI
  5V: Part1.5V, NEOPIXEL4.+5V, DS3.VDD, R4.leg1, R3.Pin_0
  N3: Part1.A0, R4.wiper

custom parts:
  Neopixel Strip -- Black (60/m): Neopixel Strip, Black, 60 pixels per meter.
